# Fritzing sketch 2-led-arduino (saved by Fritzing 0.9.3b)
breadboards: 1

parts:
  Part1 = Arduino Uno (Rev3) - ICSP
  LED1 = smd LED [color="Red (633nm)" package="0805 [SMD]"]
  R1 = Resistor [tolerance=±5% resistance=220 package="0402 [SMD]"]
  R2 = Resistor [tolerance=±5% resistance=220 package="0402 [SMD]"]
  LED2 = smd LED [color="Blue (505nm)" package="0805 [SMD]"]

nets:
  N1: Part1.D8, R2.Pin_0
  N2: Part1.D7, R1.Pin_0
  N3: Part1.GND, LED1.cathode, LED2.cathode
  N4: LED1.anode, R1.Pin_1
  N5: R2.Pin_1, LED2.anode

notes:
  Remember the positive side goes toward the electricity and the negative side goes toward ground.
